# Fritzing sketch wiring (saved by Fritzing 0.9.9b)

parts:
  Composant1 = Arduino Uno (Rev3) - ICSP
  J1 = Basic Servo
  LCM1602_IIC2 = LCM1602 IIC [part_number="LCM1602 IIC" chip_label="LCM1602 IIC" package="DIP (Dual Inline) [THT]"]
  LCD2 = LCD screen
  KEYPAD1 = Membrane Matrix Keypad

nets:
  N1: Composant1.A1, KEYPAD1.7
  N2: Composant1.A2, KEYPAD1.6
  N3: Composant1.A3, KEYPAD1.5
  N4: Composant1.A4/SDA, LCM1602_IIC2.SDA
  N5: Composant1.A5/SCL, LCM1602_IIC2.SCL
  N6: Composant1.D3_PWM, KEYPAD1.4
  N7: Composant1.D4, KEYPAD1.3
  N8: Composant1.D5_PWM, KEYPAD1.2
  N9: Composant1.D6_PWM, KEYPAD1.1
  VCC: Composant1.5V, J1.vcc, LCM1602_IIC2.VCC
  GND: Composant1.GND, J1.gnd, LCM1602_IIC2.GND
  VSS: LCM1602_IIC2.VSS, LCD2.VSS
  VDD: LCM1602_IIC2.VDD, LCD2.VDD
  N10: LCM1602_IIC2.V0, LCD2.V0
  N11: LCM1602_IIC2.RS, LCD2.RS
  N12: LCM1602_IIC2.RW, LCD2.R/W
  N13: LCM1602_IIC2.E, LCD2.E
  N14: LCM1602_IIC2.D0, LCD2.DB0
  N15: LCM1602_IIC2.D1, LCD2.DB1
  N16: LCM1602_IIC2.D2, LCD2.DB2
  N17: LCM1602_IIC2.D3, LCD2.DB3
  N18: LCM1602_IIC2.D4, LCD2.DB4
  N19: LCM1602_IIC2.D5, LCD2.DB5
  N20: LCM1602_IIC2.D6, LCD2.DB6
  N21: LCM1602_IIC2.D7, LCD2.DB7
  N22: LCM1602_IIC2.A, LCD2.LED+
  N23: LCM1602_IIC2.K, LCD2.LED-

custom parts:
  LCM1602 IIC: I2C-Module to use a 1602 or 2004 LCD on with the wire.h libory Serial LCD Modul
  Membrane Matrix Keypad: Membrane Matrix 3x4 Keypad
